# Fritzing sketch electric_sketch (saved by Fritzing 0.9.3b)

parts:
  U1 = RELAY [package=relay-jzc]
  U2 = RELAY [package=relay-jzc]
  U3 = RELAY [package=relay-jzc]
  U4 = RELAY [package=relay-jzc]  # not connected
  Part1 = Arduino Uno (Rev3)
  U5 = M10X2 [package=2x10_lock]
  U6 = Vibration Motor- ROB-08449 [package=vibe-motor-10mm]
  U7 = Vibration Motor- ROB-08449 [package=vibe-motor-10mm]
  U8 = Vibration Motor- ROB-08449 [package=vibe-motor-10mm]
  BAT1 = BC9VPC [package=bc9vpc]

nets:
  N1: U1.COIL2, U5.16
  N2: U1.NC, U6.-
  N3: U1.MAIN, Part1.D3_PWM
  N4: U1.COIL1, Part1.D2
  N5: U2.COIL2, U5.18
  N6: U2.NC, U7.-
  N7: U3.COIL2, U5.20
  N8: U3.NC, U8.-
  N9: U5.1, BAT1.V-
  N10: U5.2, BAT1.V+
  N11: U5.15, U6.+
  N12: U5.17, U7.+
  N13: U5.19, U8.+
